// Logisim project FlipFlopsRegisters.circ as structural Verilog: 3 circuits, main circuit main
module main (
  input  in_1,
  output [7:0] out_2
);

  wire clock_1_out;
  wire [7:0] adder_1_out;

  Clock clock_1 (.out(clock_1_out));
  Adder adder_1 (.a(8'h1), .b(out_2), .out(adder_1_out));  // open: cin, cout
  Register register_1 (.Reset(in_1), .Clock(clock_1_out), .Data(adder_1_out), .Q(out_2));
endmodule

module D_Type_Flip_Flop (
  input  Reset,
  input  Data,
  input  Clock,
  output Q,
  output NOT_Q
);

  wire and_1_out, and_2_out, and_3_out, and_4_out, nor_1_out, nor_2_out, not_1_out, not_2_out, or_1_out;

  not not_1 (not_1_out, Clock);
  not not_2 (not_2_out, Data);
  and and_1 (and_1_out, Data, not_1_out);
  and and_2 (and_2_out, not_1_out, not_2_out);
  nor nor_1 (nor_1_out, and_1_out, nor_2_out);
  nor nor_2 (nor_2_out, nor_1_out, and_2_out);
  and and_3 (and_3_out, nor_1_out, Clock);
  and and_4 (and_4_out, Clock, nor_2_out);
  or or_1 (or_1_out, Reset, and_3_out);
  nor nor_3 (Q, or_1_out, NOT_Q);
  nor nor_4 (NOT_Q, Q, and_4_out);
endmodule

module Register (
  input  Reset,
  input  Clock,
  input  [7:0] Data,
  output [7:0] Q
);

  D_Type_Flip_Flop d_type_flip_flop_1 (.Reset(Reset), .Data(Data[0]), .Clock(Clock), .Q(Q[0]));  // open: NOT_Q
  D_Type_Flip_Flop d_type_flip_flop_2 (.Reset(Reset), .Data(Data[1]), .Clock(Clock), .Q(Q[1]));  // open: NOT_Q
  D_Type_Flip_Flop d_type_flip_flop_3 (.Reset(Reset), .Data(Data[2]), .Clock(Clock), .Q(Q[2]));  // open: NOT_Q
  D_Type_Flip_Flop d_type_flip_flop_4 (.Reset(Reset), .Data(Data[3]), .Clock(Clock), .Q(Q[3]));  // open: NOT_Q
  D_Type_Flip_Flop d_type_flip_flop_5 (.Reset(Reset), .Data(Data[4]), .Clock(Clock), .Q(Q[4]));  // open: NOT_Q
  D_Type_Flip_Flop d_type_flip_flop_6 (.Reset(Reset), .Data(Data[5]), .Clock(Clock), .Q(Q[5]));  // open: NOT_Q
  D_Type_Flip_Flop d_type_flip_flop_7 (.Reset(Reset), .Data(Data[6]), .Clock(Clock), .Q(Q[6]));  // open: NOT_Q
  D_Type_Flip_Flop d_type_flip_flop_8 (.Reset(Reset), .Data(Data[7]), .Clock(Clock), .Q(Q[7]));  // open: NOT_Q
endmodule
