// Logisim project RockPaperSissorsLab.circ as structural Verilog: 1 circuit, main circuit main
module main (
  input  S2,
  input  P2,
  input  R2,
  input  R1,
  input  P1,
  input  S1
);

  wire transistor_1_out, transistor_2_out, transistor_3_out, transistor_4_out, transistor_5_out;

  Transistor #(.\type ("n")) transistor_1 (.in(1'b1), .out(transistor_1_out), .gate(R1));
  Transistor #(.\type ("n")) transistor_2 (.in(1'b1), .out(transistor_2_out), .gate(P1));
  Transistor #(.\type ("n")) transistor_3 (.in(1'b1), .out(transistor_3_out), .gate(S1));
  Transistor #(.\type ("n")) transistor_4 (.in(transistor_1_out), .out(transistor_4_out), .gate(S2));
  Transistor #(.\type ("n")) transistor_5 (.in(transistor_1_out), .out(transistor_5_out), .gate(P2));
  Transistor #(.\type ("n")) transistor_6 (.in(transistor_2_out), .out(transistor_4_out), .gate(R2));
  Transistor #(.\type ("n")) transistor_7 (.in(transistor_2_out), .out(transistor_5_out), .gate(S2));
  Transistor #(.\type ("n")) transistor_8 (.in(transistor_3_out), .out(transistor_4_out), .gate(P2));
  Transistor #(.\type ("n")) transistor_9 (.in(transistor_3_out), .out(transistor_5_out), .gate(R2));
  LED u_P1 (.in(transistor_4_out));
  LED u_P2 (.in(transistor_5_out));
endmodule
