// Logisim project SimpleLogicUnit.circ as structural Verilog: 2 circuits, main circuit main
module main (
  input  [7:0] in_1,
  input  [7:0] in_2,
  input  [1:0] in_3,
  output [7:0] out_4
);

  Logic_Unit logic_unit_1 (.input1(in_2), .input0(in_1), .\logic (in_3), .\output (out_4));
endmodule

module Logic_Unit (
  input  [7:0] input1,
  input  [7:0] input0,
  input  [1:0] \logic ,
  output [7:0] \output 
);

  wire [7:0] and_out, not_out, or_out, xor_out;

  assign and_out = input1 & input0;  // AND_Gate and, 8 bits wide
  assign or_out = input1 | input0;  // OR_Gate or, 8 bits wide
  assign xor_out = input1 ^ input0;  // XOR_Gate xor, 8 bits wide
  assign not_out = ~input1;  // NOT_Gate not, 8 bits wide
  Multiplexer #(.select(2), .width(8), .enable("false")) multiplexer_1 (
    .in0(and_out), .in1(or_out), .in2(xor_out), .in3(not_out), .out(\output ), .sel(\logic ));
endmodule
