// Logisim project GateLab1.circ as structural Verilog: 1 circuit, main circuit main
module main (
  input  a,
  input  b,
  input  c
);

  wire _0_out, _1_out, _2_out, _3_out, _4_out, _5_out, _6_out, _7_out, BLeft_out, Bottom_out, BRight_out,
       Middle_out, TLeft_out, Top_out, TRight_out;

  and _0 (_0_out, ~c, ~b, ~a);  // AND_Gate
  and _1 (_1_out, c, ~b, ~a);  // AND_Gate
  and _2 (_2_out, ~c, b, ~a);  // AND_Gate
  and _3 (_3_out, c, b, ~a);  // AND_Gate
  and _3_2 (_3_out, c, b, ~a);  // AND_Gate
  and _4 (_4_out, ~c, ~b, a);  // AND_Gate
  and _5 (_5_out, c, ~b, a);  // AND_Gate
  and _6 (_6_out, ~c, b, a);  // AND_Gate
  and _7 (_7_out, c, b, a);
  or Middle (Middle_out, _2_out, _3_out, _4_out);
  buf BLeft (BLeft_out, _2_out);  // OR_Gate
  or TLeft (TLeft_out, _0_out, _4_out);
  or Bottom (Bottom_out, _0_out, _2_out, _3_out);
  _7_Segment_Display u_7_segment_display_1 (
    .g(Middle_out), .f(TLeft_out), .a(Top_out), .b(TRight_out), .e(BLeft_out), .d(Bottom_out), .c(BRight_out));  // open: dp
  or Top (Top_out, _0_out, _2_out, _3_out);
  or BRight (BRight_out, _0_out, _1_out, _3_out, _4_out, _7_out);
  or TRight (TRight_out, _0_out, _1_out, _2_out, _3_out, _4_out);
endmodule
