// Logisim project GateLab3.circ as structural Verilog: 1 circuit, main circuit main
module main (
  input  a,
  input  b,
  input  c,
  input  d
);

  wire _0_out, _1_out, _2_out, _3_out, _4_out, _5_out, _6_out, _7_out, _8_out, _9_out, BLeft_out, Bottom_out,
       BRight_out, Middle_out, TLeft_out, Top_out, TRight_out;

  and _0 (_0_out, ~d, ~c, ~b, ~a);  // AND_Gate
  and _1 (_1_out, d, ~c, ~b, ~a);  // AND_Gate
  and _2 (_2_out, ~d, c, ~b, ~a);  // AND_Gate
  and _3 (_3_out, d, c, ~b);  // AND_Gate
  and _4 (_4_out, ~d, ~c, b, ~a);  // AND_Gate
  and _5 (_5_out, d, ~c, b);  // AND_Gate
  and _6 (_6_out, ~d, c, b, ~a);  // AND_Gate
  and _7 (_7_out, d, c, b);  // AND_Gate
  and _8 (_8_out, ~d, ~c, ~b, a);  // AND_Gate
  and _9 (_9_out, d, ~c, ~b, a);  // AND_Gate
  or Middle (Middle_out, _2_out, _3_out, _4_out, _5_out, _6_out, _8_out, _9_out);
  or BLeft (BLeft_out, _0_out, _2_out, _6_out, _8_out);
  or Bottom (Bottom_out, _0_out, _2_out, _3_out, _5_out, _6_out, _8_out);
  or TLeft (TLeft_out, _0_out, _4_out, _5_out, _6_out, _8_out, _9_out);
  _7_Segment_Display u_7_segment_display_1 (
    .g(Middle_out), .f(TLeft_out), .a(Top_out), .b(TRight_out), .e(BLeft_out), .d(Bottom_out), .c(BRight_out));  // open: dp
  or Top (Top_out, _0_out, _2_out, _3_out, _5_out, _6_out, _7_out, _8_out, _9_out);
  or BRight (BRight_out, _0_out, _1_out, _3_out, _4_out, _5_out, _6_out, _7_out, _8_out, _9_out);
  or TRight (TRight_out, _0_out, _1_out, _2_out, _3_out, _4_out, _7_out, _8_out, _9_out);
endmodule
