// Logisim project Computer.circ as structural Verilog: 9 circuits, main circuit main
module main (
  input  Clear
);

  wire A_out, and_1_out, B_out, button_2_out, button_3_out, button_out, clock_1_out,
       memory_comparator_1_button_state, memory_comparator_1_ram, memory_comparator_1_vram,
       opcode_comparator_1_branch, opcode_comparator_1_i, opcode_comparator_1_load,
       opcode_comparator_1_store, opcode_comparator_1_write, or_1_out, v_out;
  wire [3:0] bit_extender_2_out, decoder_1_dest, decoder_1_src1, decoder_1_src2, multiplexer_2_out, opcode;
  wire [14:0] bit_extender_1_out;
  wire [15:0] arithmetic_logic_unit_1_output, BSR, fetcher_1_out, immed, Memory, multiplexer_1_out,
       multiplexer_3_out, multiplexer_4_out, multiplexer_5_out, ram_1_data, screen_memory_1_out1,
       screen_memory_1_out2, screen_memory_1_out3, screen_memory_1_out4, screen_memory_1_out5,
       screen_memory_1_out6, screen_memory_1_out7, screen_memory_1_out8, screen_memory_1_out9,
       screen_memory_1_out10, screen_memory_1_out11, screen_memory_1_out12, screen_memory_1_out13,
       screen_memory_1_out14, screen_memory_1_out15, screen_memory_1_out16, SRC2;

  Clock clock_1 (.out(clock_1_out));
  // Probe on fetcher_1_out
  Fetcher fetcher_1 (
    .Value(immed), .Out(fetcher_1_out), .Branch(opcode_comparator_1_branch), .Clock(clock_1_out),
    .Clear(Clear));
  // Probe on opcode
  Decoder decoder_1 (
    .Data(fetcher_1_out), .Opcode(opcode), .Dest(decoder_1_dest), .SRC1(decoder_1_src1),
    .SRC2(decoder_1_src2), .Immed(immed));
  Memory_Comparator memory_comparator_1 (
    .Memory(Memory), .Store(opcode_comparator_1_store), .RAM(memory_comparator_1_ram),
    .VRAM(memory_comparator_1_vram), .Button_State(memory_comparator_1_button_state));
  Opcode_Comparator opcode_comparator_1 (
    .Opcode(opcode), .Load(opcode_comparator_1_load), .Store(opcode_comparator_1_store),
    .Write(opcode_comparator_1_write), .I(opcode_comparator_1_i), .Branch(opcode_comparator_1_branch),
    .BranchChecker(arithmetic_logic_unit_1_output));
  Multiplexer #(.width(16), .enable("false")) multiplexer_1 (
    .in0(arithmetic_logic_unit_1_output), .in1(multiplexer_3_out), .out(multiplexer_1_out),
    .sel(opcode_comparator_1_load));
  Button button (.out(button_out));
  Button button_2 (.out(button_2_out));
  Button v (.out(v_out));
  Bit_Extender #(.in_width(16), .out_width(15)) bit_extender_1 (.in(Memory), .out(bit_extender_1_out));
  Button B (.out(B_out));
  Button button_3 (.out(button_3_out));
  Multiplexer #(.width(4), .enable("false")) multiplexer_2 (
    .in0(decoder_1_src1), .in1(decoder_1_dest), .out(multiplexer_2_out), .sel(opcode_comparator_1_i));
  or or_1 (or_1_out, opcode_comparator_1_load, memory_comparator_1_ram);
  Button A (.out(A_out));
  Button_State_Register button_state_register_1 (
    .A(A_out), .B(B_out), .Right(button_3_out), .Left(button_2_out), .Up(button_out), .Down(v_out),
    .out_7(BSR));
  Register_File register_file_1 (
    .Read_Value_1(Memory), .Read_Address_1(multiplexer_2_out), .Write_Data(multiplexer_1_out),
    .Clock(clock_1_out), .Write_Address(decoder_1_dest), .Read_Value_2(SRC2),
    .Read_Address_2(decoder_1_src2), .Clear(Clear), .Write_Enable(opcode_comparator_1_write));
  RAM #(.addrWidth(15), .dataWidth(16), .bus("separate")) ram_1 (
    .addr(bit_extender_1_out), .din(SRC2), .data(ram_1_data), .str(memory_comparator_1_ram), .sel(or_1_out),
    .clk(clock_1_out), .ld(opcode_comparator_1_load), .clr(opcode_comparator_1_load));
  Multiplexer #(.width(16), .enable("false")) multiplexer_3 (
    .in0(ram_1_data), .in1(multiplexer_5_out), .out(multiplexer_3_out), .sel(memory_comparator_1_button_state));
  Arithmetic_Logic_Unit arithmetic_logic_unit_1 (
    .\output (arithmetic_logic_unit_1_output), .in1(Memory), .in2(multiplexer_4_out), .opcode(opcode));
  Multiplexer #(.width(16), .enable("false")) multiplexer_4 (
    .in0(SRC2), .in1(immed), .out(multiplexer_4_out), .sel(opcode_comparator_1_i));
  and and_1 (and_1_out, opcode_comparator_1_store, memory_comparator_1_button_state);
  Bit_Extender #(.in_width(16), .out_width(4)) bit_extender_2 (.in(Memory), .out(bit_extender_2_out));
  Multiplexer #(.width(16), .enable("false")) multiplexer_5 (
    .in0(BSR), .in1(SRC2), .out(multiplexer_5_out), .sel(and_1_out));
  Screen_Memory screen_memory_1 (
    .Write_Data(SRC2), .Clock(clock_1_out), .Write_Address(bit_extender_2_out), .out1(screen_memory_1_out1),
    .out2(screen_memory_1_out2), .out3(screen_memory_1_out3), .out4(screen_memory_1_out4),
    .out5(screen_memory_1_out5), .out6(screen_memory_1_out6), .out7(screen_memory_1_out7),
    .out8(screen_memory_1_out8), .out9(screen_memory_1_out9), .out10(screen_memory_1_out10),
    .out11(screen_memory_1_out11), .out12(screen_memory_1_out12), .out13(screen_memory_1_out13),
    .out14(screen_memory_1_out14), .out15(screen_memory_1_out15), .out16(screen_memory_1_out16),
    .Clear(Clear), .Write_Enable(memory_comparator_1_vram));
  DotMatrix #(.inputtype("row"), .matrixcols(16), .matrixrows(16)) dotmatrix_1 (
    .row0(screen_memory_1_out1), .row1(screen_memory_1_out2), .row2(screen_memory_1_out3),
    .row3(screen_memory_1_out4), .row4(screen_memory_1_out5), .row5(screen_memory_1_out6),
    .row6(screen_memory_1_out7), .row7(screen_memory_1_out8), .row8(screen_memory_1_out9),
    .row9(screen_memory_1_out10), .row10(screen_memory_1_out11), .row11(screen_memory_1_out12),
    .row12(screen_memory_1_out13), .row13(screen_memory_1_out14), .row14(screen_memory_1_out15),
    .row15(screen_memory_1_out16));
endmodule

// ALU
module Arithmetic_Logic_Unit (
  input  [15:0] in1,
  input  [15:0] in2,
  input  [3:0] opcode,
  output [15:0] \output 
);

  wire _1_2_out, comparator_1_lt, comparator_2_eq, comparator_2_gt, comparator_2_lt;
  wire [3:0] bit_extender_1_out, bit_extender_2_out;
  wire [15:0] _0_out, _1_out, _2_out, adder_1_out, bit_extender_3_out, bit_extender_4_out,
       bit_extender_5_out, multiplier_1_out, not_1_out, shifter_1_out, shifter_2_out, subtractor_1_out;

  assign _0_out = in2 & in1;  // AND_Gate _0, 16 bits wide
  assign _1_out = in2 | in1;  // OR_Gate _1, 16 bits wide
  assign _2_out = in2 ^ in1;  // XOR_Gate _2, 16 bits wide
  Adder #(.width(16)) adder_1 (.a(in2), .b(in1), .out(adder_1_out));  // open: cin, cout
  Subtractor #(.width(16)) subtractor_1 (.a(in1), .b(in2), .out(subtractor_1_out));  // open: bin, bout
  Multiplier #(.width(16)) multiplier_1 (.a(in2), .b(in1), .out(multiplier_1_out));  // open: cin, cout
  Comparator #(.width(16)) comparator_1 (.a(in1), .b(in2), .lt(comparator_1_lt));  // open: gt, eq
  Bit_Extender #(.in_width(16), .out_width(4)) bit_extender_1 (.in(in2), .out(bit_extender_1_out));
  Bit_Extender #(.in_width(16), .out_width(4)) bit_extender_2 (.in(in2), .out(bit_extender_2_out));
  Comparator #(.width(16)) comparator_2 (
    .a(in1), .b({16{1'b0}}), .gt(comparator_2_gt), .eq(comparator_2_eq), .lt(comparator_2_lt));
  Shifter #(.width(16)) shifter_1 (.in(in1), .\dist (bit_extender_1_out), .out(shifter_1_out));
  Shifter #(.width(16), .shift("ar")) shifter_2 (.in(in1), .\dist (bit_extender_2_out), .out(shifter_2_out));
  assign bit_extender_3_out = {{15{1'b0}}, comparator_1_lt};  // Bit_Extender bit_extender_3
  assign bit_extender_4_out = {{15{1'b0}}, comparator_2_eq};  // Bit_Extender bit_extender_4
  or _1_2 (_1_2_out, comparator_2_gt, comparator_2_lt);
  assign bit_extender_5_out = {{15{1'b0}}, _1_2_out};  // Bit_Extender bit_extender_5
  assign not_1_out = ~in1;  // NOT_Gate not_1, 16 bits wide
  Multiplexer #(.select(4), .width(16), .enable("false")) multiplexer_1 (
    .in0(_0_out), .in1(_1_out), .in2(_2_out), .in3(not_1_out), .in4(adder_1_out), .in5(subtractor_1_out),
    .in6(multiplier_1_out), .in7(bit_extender_3_out), .in8(shifter_1_out), .in9(shifter_2_out), .in10(in1),
    .in11(in1), .in12(in2), .in13(16'h1), .in14(bit_extender_4_out), .in15(bit_extender_5_out),
    .out(\output ), .sel(opcode));
endmodule

// RF
module Register_File (
  input  [3:0] Read_Address_1,
  input  [3:0] Read_Address_2,
  input  [15:0] Write_Data,
  input  Clock,
  input  Clear,
  input  [3:0] Write_Address,
  input  Write_Enable,
  output [15:0] Read_Value_1,
  output [15:0] Read_Value_2
);

  wire decoder_1_out0, decoder_1_out1, decoder_1_out2, decoder_1_out3, decoder_1_out4, decoder_1_out5,
       decoder_1_out6, decoder_1_out7, decoder_1_out8, decoder_1_out9, decoder_1_out10, decoder_1_out11,
       decoder_1_out12, decoder_1_out13, decoder_1_out14, decoder_1_out15;
  wire [15:0] register_1_q, register_2_q, register_3_q, register_4_q, register_5_q, register_6_q,
       register_7_q, register_8_q, register_9_q, register_10_q, register_11_q, register_12_q, register_13_q,
       register_14_q, register_15_q, register_16_q;

  Register #(.width(16)) register_1 (.D(Write_Data), .en(decoder_1_out0), .Q(register_1_q), .clk(Clock), .clr(Clear));
  Register #(.width(16)) register_2 (.D(Write_Data), .en(decoder_1_out1), .Q(register_2_q), .clk(Clock), .clr(Clear));
  Register #(.width(16)) register_3 (.D(Write_Data), .en(decoder_1_out2), .Q(register_3_q), .clk(Clock), .clr(Clear));
  Register #(.width(16)) register_4 (.D(Write_Data), .en(decoder_1_out4), .Q(register_4_q), .clk(Clock), .clr(Clear));
  Register #(.width(16)) register_5 (.D(Write_Data), .en(decoder_1_out3), .Q(register_5_q), .clk(Clock), .clr(Clear));
  Multiplexer #(.select(4), .width(16), .enable("false")) multiplexer_1 (
    .in0(register_1_q), .in1(register_2_q), .in2(register_3_q), .in3(register_5_q), .in4(register_4_q),
    .in5(register_6_q), .in6(register_7_q), .in7(register_8_q), .in8(register_10_q), .in9(register_9_q),
    .in10(register_11_q), .in11(register_12_q), .in12(register_13_q), .in13(register_14_q),
    .in14(register_15_q), .in15(register_16_q), .out(Read_Value_1), .sel(Read_Address_1));
  Register #(.width(16)) register_6 (.D(Write_Data), .en(decoder_1_out5), .Q(register_6_q), .clk(Clock), .clr(Clear));
  Register #(.width(16)) register_7 (.D(Write_Data), .en(decoder_1_out6), .Q(register_7_q), .clk(Clock), .clr(Clear));
  Decoder_part #(.select(4), .disabled(0)) decoder_1 (
    .out0(decoder_1_out0), .out1(decoder_1_out1), .out2(decoder_1_out2), .out3(decoder_1_out3),
    .out4(decoder_1_out4), .out5(decoder_1_out5), .out6(decoder_1_out6), .out7(decoder_1_out7),
    .out8(decoder_1_out8), .out9(decoder_1_out9), .out10(decoder_1_out10), .out11(decoder_1_out11),
    .out12(decoder_1_out12), .out13(decoder_1_out13), .out14(decoder_1_out14), .out15(decoder_1_out15),
    .sel(Write_Address), .en(Write_Enable));
  Register #(.width(16)) register_8 (.D(Write_Data), .en(decoder_1_out7), .Q(register_8_q), .clk(Clock), .clr(Clear));
  Register #(.width(16)) register_9 (.D(Write_Data), .en(decoder_1_out9), .Q(register_9_q), .clk(Clock), .clr(Clear));
  Register #(.width(16)) register_10 (.D(Write_Data), .en(decoder_1_out8), .Q(register_10_q), .clk(Clock), .clr(Clear));
  Multiplexer #(.select(4), .width(16), .enable("false")) multiplexer_2 (
    .in0(register_1_q), .in1(register_2_q), .in2(register_3_q), .in3(register_5_q), .in4(register_4_q),
    .in5(register_6_q), .in6(register_7_q), .in7(register_8_q), .in8(register_10_q), .in9(register_9_q),
    .in10(register_11_q), .in11(register_12_q), .in12(register_13_q), .in13(register_14_q),
    .in14(register_15_q), .in15(register_16_q), .out(Read_Value_2), .sel(Read_Address_2));
  Register #(.width(16)) register_11 (
    .D(Write_Data), .en(decoder_1_out10), .Q(register_11_q), .clk(Clock), .clr(Clear));
  Register #(.width(16)) register_12 (
    .D(Write_Data), .en(decoder_1_out11), .Q(register_12_q), .clk(Clock), .clr(Clear));
  Register #(.width(16)) register_13 (
    .D(Write_Data), .en(decoder_1_out12), .Q(register_13_q), .clk(Clock), .clr(Clear));
  Register #(.width(16)) register_14 (
    .D(Write_Data), .en(decoder_1_out13), .Q(register_14_q), .clk(Clock), .clr(Clear));
  Register #(.width(16)) register_15 (
    .D(Write_Data), .en(decoder_1_out14), .Q(register_15_q), .clk(Clock), .clr(Clear));
  Register #(.width(16)) register_16 (
    .D(Write_Data), .en(decoder_1_out15), .Q(register_16_q), .clk(Clock), .clr(Clear));
endmodule

// SM
module Screen_Memory (
  input  [15:0] Write_Data,
  input  Clock,
  input  Clear,
  input  [3:0] Write_Address,
  input  Write_Enable,
  output [15:0] out1,
  output [15:0] out3,
  output [15:0] out5,
  output [15:0] out7,
  output [15:0] out9,
  output [15:0] out11,
  output [15:0] out13,
  output [15:0] out15,
  output [15:0] out2,
  output [15:0] out4,
  output [15:0] out6,
  output [15:0] out8,
  output [15:0] out10,
  output [15:0] out12,
  output [15:0] out14,
  output [15:0] out16
);

  wire decoder_1_out0, decoder_1_out1, decoder_1_out2, decoder_1_out3, decoder_1_out4, decoder_1_out5,
       decoder_1_out6, decoder_1_out7, decoder_1_out8, decoder_1_out9, decoder_1_out10, decoder_1_out11,
       decoder_1_out12, decoder_1_out13, decoder_1_out14, decoder_1_out15;

  Register #(.width(16)) register_1 (.D(Write_Data), .en(decoder_1_out0), .Q(out1), .clk(Clock), .clr(Clear));
  Register #(.width(16)) register_2 (.D(Write_Data), .en(decoder_1_out1), .Q(out2), .clk(Clock), .clr(Clear));
  Register #(.width(16)) register_3 (.D(Write_Data), .en(decoder_1_out2), .Q(out3), .clk(Clock), .clr(Clear));
  Register #(.width(16)) register_4 (.D(Write_Data), .en(decoder_1_out4), .Q(out5), .clk(Clock), .clr(Clear));
  Register #(.width(16)) register_5 (.D(Write_Data), .en(decoder_1_out3), .Q(out4), .clk(Clock), .clr(Clear));
  Register #(.width(16)) register_6 (.D(Write_Data), .en(decoder_1_out5), .Q(out6), .clk(Clock), .clr(Clear));
  Register #(.width(16)) register_7 (.D(Write_Data), .en(decoder_1_out6), .Q(out7), .clk(Clock), .clr(Clear));
  Decoder_part #(.select(4), .disabled(0)) decoder_1 (
    .out0(decoder_1_out0), .out1(decoder_1_out1), .out2(decoder_1_out2), .out3(decoder_1_out3),
    .out4(decoder_1_out4), .out5(decoder_1_out5), .out6(decoder_1_out6), .out7(decoder_1_out7),
    .out8(decoder_1_out8), .out9(decoder_1_out9), .out10(decoder_1_out10), .out11(decoder_1_out11),
    .out12(decoder_1_out12), .out13(decoder_1_out13), .out14(decoder_1_out14), .out15(decoder_1_out15),
    .sel(Write_Address), .en(Write_Enable));
  Register #(.width(16)) register_8 (.D(Write_Data), .en(decoder_1_out7), .Q(out8), .clk(Clock), .clr(Clear));
  Register #(.width(16)) register_9 (.D(Write_Data), .en(decoder_1_out8), .Q(out9), .clk(Clock), .clr(Clear));
  Register #(.width(16)) register_10 (.D(Write_Data), .en(decoder_1_out9), .Q(out10), .clk(Clock), .clr(Clear));
  Register #(.width(16)) register_11 (.D(Write_Data), .en(decoder_1_out10), .Q(out11), .clk(Clock), .clr(Clear));
  Register #(.width(16)) register_12 (.D(Write_Data), .en(decoder_1_out12), .Q(out13), .clk(Clock), .clr(Clear));
  Register #(.width(16)) register_13 (.D(Write_Data), .en(decoder_1_out11), .Q(out12), .clk(Clock), .clr(Clear));
  Register #(.width(16)) register_14 (.D(Write_Data), .en(decoder_1_out13), .Q(out14), .clk(Clock), .clr(Clear));
  Register #(.width(16)) register_15 (.D(Write_Data), .en(decoder_1_out14), .Q(out15), .clk(Clock), .clr(Clear));
  Register #(.width(16)) register_16 (.D(Write_Data), .en(decoder_1_out15), .Q(out16), .clk(Clock), .clr(Clear));
endmodule

// Fetch
module Fetcher (
  input  Branch,
  input  [15:0] Value,
  input  Clock,
  input  Clear,
  output [15:0] Out
);

  wire [15:0] adder_1_out, multiplexer_1_out, register_1_q;

  // Probe on register_1_q
  Register #(.width(16)) register_1 (.D(adder_1_out), .Q(register_1_q), .clk(Clock), .clr(Clear));  // open: en
  Multiplexer #(.width(16), .enable("false")) multiplexer_1 (
    .in0(16'h1), .in1(Value), .out(multiplexer_1_out), .sel(Branch));
  ROM #(.addrWidth(16), .dataWidth(16)) rom_1 (.addr(register_1_q), .data(Out));  // open: sel
  Adder #(.width(16)) adder_1 (.a(multiplexer_1_out), .b(register_1_q), .out(adder_1_out));  // open: cin, cout

  // Notes on the sheet:
  //   contents of rom_1 (hex, n*v repeats v):
  //   c080 c108 8001 ce10 4e0e c20f c90f c301 c401 c540 cb08 855b e70c a22 5226 5664 110a b018 5114 b018
  //   7b92 eb03 c700 299 1102 b013 5114 b013 ade0 cc04 bdc fb08 cc08 bdc fb0d cc10 bdc fb0e d0e6 b34 fbe4
  //   b03 fb03 9334 d0e0 355 d0de b03 fbdc 8334 d0da f7d9 c701 c602 d0d6
endmodule

module Decoder (
  input  [15:0] Data,
  output [15:0] Immed,
  output [3:0] SRC1,
  output [3:0] SRC2,
  output [3:0] Opcode,
  output [3:0] Dest
);

  assign Immed = {{8{Data[7]}}, Data[7:0]};  // Bit_Extender bit_extender_1

  assign Dest = Data[11:8];
  assign Opcode = Data[15:12];
  assign SRC1 = Data[7:4];
  assign SRC2 = Data[3:0];
endmodule

// BSR
module Button_State_Register (
  input  A,
  input  B,
  input  Right,
  input  Left,
  input  Up,
  input  Down,
  output [15:0] out_7
);

  assign out_7 = {{10{1'b0}}, {Down, Up, Left, Right, B, A}};  // Bit_Extender bit_extender_1
endmodule

// Op
module Opcode_Comparator (
  input  [15:0] BranchChecker,
  input  [3:0] Opcode,
  output Load,
  output Store,
  output Write,
  output I,
  output Branch
);

  wire and_1_out, bit_extender_1_out, comparator_2_lt, comparator_3_eq, comparator_3_gt, comparator_4_eq,
       comparator_4_gt;

  Comparator #(.width(4), .mode("unsigned")) comparator_1 (.a(Opcode), .b(4'b1010), .eq(Load));  // open: gt, lt
  Comparator #(.width(4), .mode("unsigned")) comparator_2 (
    .a(Opcode), .b(4'b1011), .eq(Store), .lt(comparator_2_lt));  // open: gt
  Bit_Extender #(.in_width(16), .out_width(1)) bit_extender_1 (.in(BranchChecker), .out(bit_extender_1_out));
  Comparator #(.width(4), .mode("unsigned")) comparator_3 (
    .a(Opcode), .b(4'b1100), .gt(comparator_3_gt), .eq(comparator_3_eq));  // open: lt
  or u_I (I, comparator_3_eq, comparator_3_gt);
  or Wr (Write, comparator_2_lt, comparator_3_eq);
  Comparator #(.width(4), .mode("unsigned")) comparator_4 (
    .a(Opcode), .b(4'b1101), .gt(comparator_4_gt), .eq(comparator_4_eq));  // open: lt
  and and_1 (and_1_out, comparator_4_gt, bit_extender_1_out);
  or or_1 (Branch, comparator_4_eq, and_1_out);

  // Notes on the sheet:
  //   0 - 10: WRITE ENABLE
endmodule

// Mem.
module Memory_Comparator (
  input  Store,
  input  [15:0] Memory,
  output RAM,
  output VRAM,
  output Button_State
);

  wire and_1_out, comparator_1_eq, comparator_1_gt, comparator_1_lt, comparator_2_eq, comparator_2_lt,
       or_1_out, or_2_out, or_3_out;

  or or_1 (or_1_out, comparator_1_gt, comparator_1_eq);
  Comparator #(.width(16), .mode("unsigned")) comparator_1 (
    .a(Memory), .b(16'h8000), .gt(comparator_1_gt), .eq(comparator_1_eq), .lt(comparator_1_lt));
  Comparator #(.width(16), .mode("unsigned")) comparator_2 (
    .a(Memory), .b(16'h800f), .eq(comparator_2_eq), .lt(comparator_2_lt));  // open: gt
  or or_2 (or_2_out, comparator_2_eq, comparator_2_lt);
  Comparator #(.width(16), .mode("unsigned")) comparator_3 (
    .a(Memory), .b(16'h8010), .eq(Button_State));  // open: gt, lt
  or or_3 (or_3_out, comparator_1_eq, comparator_1_lt);
  and and_1 (and_1_out, or_1_out, or_2_out);
  and and_2 (RAM, Store, or_3_out);
  and and_3 (VRAM, Store, and_1_out);
endmodule
